# Fritzing sketch DHT11 Serial (saved by Fritzing 0.9.1b)

parts:
  Part1 = Arduino Uno (Rev3)
  RHT1 = Humidity and Temperature Sensor RHT03
  R1 = Resistor [tolerance=±5% resistance=100k package="0805 [SMD]"]

nets:
  N1: Part1.D2, RHT1.Data-signal, R1.Pin_0
  5V: Part1.5V, RHT1.Vcc, R1.Pin_1
  N2: Part1.GND, RHT1.GND_2
