# Fritzing sketch DS18B20 Serial (saved by Fritzing 0.9.1b)

parts:
  Part1 = Arduino Uno (Rev3)
  R1 = Resistor [tolerance=±5% resistance=4.7k package="0805 [SMD]"]
  DS1 = DS18B20 1-Wire Temperature Sensor [part_number=DS18B20]

nets:
  N1: Part1.D2, R1.Pin_0, DS1.DQ
  5V: Part1.5V, DS1.VDD
  GND: Part1.GND, DS1.GND
